// Logisim project Basic Computer.circ as structural Verilog: 14 circuits, main circuit main
module main (
  input  [7:0] INPR
);

  wire alu_1_e, and_1_out, CLK_out, control_unit_1_acclr, control_unit_1_acinr, control_unit_1_acload,
       control_unit_1_arinr, control_unit_1_arload, control_unit_1_dcinr, control_unit_1_drload,
       control_unit_1_eclr, control_unit_1_ecmp, control_unit_1_eload, control_unit_1_fgi_2,
       control_unit_1_fgiload, control_unit_1_fgo_2, control_unit_1_fgoload, control_unit_1_hlt,
       control_unit_1_ien, control_unit_1_ienload, control_unit_1_inpload, control_unit_1_irload,
       control_unit_1_mload, control_unit_1_outrload, control_unit_1_pcinr, control_unit_1_pcload, d_ff_1_q,
       d_ff_1_qn, e_flag_1_q, FGI_q, FGO_q, RESET_out;
  wire [2:0] control_unit_1_regsel;
  wire [4:0] control_unit_1_opr;
  wire [7:0] bit_extender_1_out;
  wire [11:0] AR_data_output__12;
  wire [15:0] AC_data_output, alu_1_out_7, AR_data_output__16, DR_data_output, IR_data_output,
       multiplexer_1_out, PC_data_output__16, ram_1_data, TR_data_output;

  Button RESET (.out(RESET_out));
  Clock CLK (.out(CLK_out));
  LED led_1 (.in(d_ff_1_q));
  LED led_2 (.in(d_ff_1_qn));
  and and_1 (and_1_out, CLK_out, d_ff_1_qn);
  D_Flip_Flop d_ff_1 (
    .Q(d_ff_1_q), .Qn(d_ff_1_qn), .preset(control_unit_1_hlt), .reset(RESET_out));  // open: clk, D, en
  Control_Unit control_unit_1 (
    .IR(IR_data_output), .CLK(and_1_out), .REGSEL(control_unit_1_regsel), .ELOAD(control_unit_1_eload),
    .ARLOAD(control_unit_1_arload), .IRLOAD(control_unit_1_irload), .MLOAD(control_unit_1_mload),
    .PCLOAD(control_unit_1_pcload), .PCINR(control_unit_1_pcinr), .AC(AC_data_output), .DR(DR_data_output),
    .FGI(FGI_q), .FGO(FGO_q), .RESET(RESET_out), .OPR(control_unit_1_opr), .ACLOAD(control_unit_1_acload),
    .DRLOAD(control_unit_1_drload), .ARINR(control_unit_1_arinr), .DCINR(control_unit_1_dcinr),
    .E(e_flag_1_q), .ACCLR(control_unit_1_acclr), .FGOLOAD(control_unit_1_fgoload),
    .FGO_2(control_unit_1_fgo_2), .FGILOAD(control_unit_1_fgiload), .FGI_2(control_unit_1_fgi_2),
    .INPLOAD(control_unit_1_inpload), .ACINR(control_unit_1_acinr), .ECLR(control_unit_1_eclr),
    .ECMP(control_unit_1_ecmp), .IENLOAD(control_unit_1_ienload), .IEN(control_unit_1_ien),
    .OUTRLOAD(control_unit_1_outrload), .HLT(control_unit_1_hlt));  // open: SC
  Bit_Extender #(.in_width(16), .out_width(8)) bit_extender_1 (.in(multiplexer_1_out), .out(bit_extender_1_out));
  Register OUTR (.D(bit_extender_1_out), .en(control_unit_1_outrload), .clk(and_1_out));  // open: Q, clr
  RAM #(.addrWidth(12), .dataWidth(16), .bus("separate")) ram_1 (
    .addr(AR_data_output__12), .din(multiplexer_1_out), .data(ram_1_data), .str(control_unit_1_mload),
    .clk(and_1_out));  // open: sel, ld, clr
  AR AR (
    .Data_Input(multiplexer_1_out), .Data_Output__16(AR_data_output__16), .INR(control_unit_1_arinr),
    .LD(control_unit_1_arload), .CLK(and_1_out), .CLR(RESET_out), .Data_Output__12(AR_data_output__12));
  PC PC (
    .Data_Input(multiplexer_1_out), .Data_Output__16(PC_data_output__16), .INR(control_unit_1_pcinr),
    .LD(control_unit_1_pcload), .CLK(and_1_out), .CLR(RESET_out));
  DR DR (
    .Data_Input(multiplexer_1_out), .Data_Output(DR_data_output), .INR(control_unit_1_dcinr),
    .LD(control_unit_1_drload), .CLK(and_1_out));  // open: CLR
  ALU alu_1 (
    .B(DR_data_output), .A(AC_data_output), .SHL(e_flag_1_q), .OPR(control_unit_1_opr), .SHR(e_flag_1_q),
    .out_7(alu_1_out_7), .E(alu_1_e));
  IR IR (
    .Data_Input(multiplexer_1_out), .Data_Output(IR_data_output), .LD(control_unit_1_irload), .CLK(and_1_out));  // open: INR, CLR
  TR TR (.Data_Input(multiplexer_1_out), .Data_Output(TR_data_output), .CLK(and_1_out));  // open: INR, LD, CLR
  AC AC (
    .Data_Input(alu_1_out_7), .Data_Output(AC_data_output), .INR(control_unit_1_acinr),
    .LD(control_unit_1_acload), .CLK(and_1_out), .CLR(control_unit_1_acclr), .EXTERNAL_INP(INPR),
    .INPLOAD(control_unit_1_inpload));
  Multiplexer #(.select(3), .width(16), .enable("false")) multiplexer_1 (
    .in1(AR_data_output__16), .in2(PC_data_output__16), .in3(DR_data_output), .in4(AC_data_output),
    .in5(IR_data_output), .in6(TR_data_output), .in7(ram_1_data), .out(multiplexer_1_out),
    .sel(control_unit_1_regsel));  // open: in0
  Hex_Digit_Display hex_digit_display_1 (.value(PC_data_output__16[15:12]));  // open: dp
  Hex_Digit_Display hex_digit_display_2 (.value(DR_data_output[15:12]));  // open: dp
  Hex_Digit_Display hex_digit_display_3 (.value(AC_data_output[15:12]));  // open: dp
  Hex_Digit_Display hex_digit_display_4 (.value(IR_data_output[15:12]));  // open: dp
  Hex_Digit_Display hex_digit_display_5 (.value(PC_data_output__16[11:8]));  // open: dp
  Hex_Digit_Display hex_digit_display_6 (.value(PC_data_output__16[7:4]));  // open: dp
  Hex_Digit_Display hex_digit_display_7 (.value(DR_data_output[11:8]));  // open: dp
  Hex_Digit_Display hex_digit_display_8 (.value(DR_data_output[7:4]));  // open: dp
  Hex_Digit_Display hex_digit_display_9 (.value(AC_data_output[11:8]));  // open: dp
  Hex_Digit_Display hex_digit_display_10 (.value(AC_data_output[7:4]));  // open: dp
  Hex_Digit_Display hex_digit_display_11 (.value(IR_data_output[11:8]));  // open: dp
  Hex_Digit_Display hex_digit_display_12 (.value(IR_data_output[7:4]));  // open: dp
  Hex_Digit_Display hex_digit_display_13 (.value(PC_data_output__16[3:0]));  // open: dp
  Hex_Digit_Display hex_digit_display_14 (.value(DR_data_output[3:0]));  // open: dp
  Hex_Digit_Display hex_digit_display_15 (.value(AC_data_output[3:0]));  // open: dp
  Hex_Digit_Display hex_digit_display_16 (.value(IR_data_output[3:0]));  // open: dp
  E_Flag e_flag_1 (
    .CLK(and_1_out), .E(alu_1_e), .Q(e_flag_1_q), .CMP(control_unit_1_ecmp), .LOAD(control_unit_1_eload),
    .CLR(control_unit_1_eclr));
  LED E (.in(e_flag_1_q));
  D_Flip_Flop R (.clk(and_1_out));  // open: D, Q, Qn, preset, en, reset
  D_Flip_Flop FGI (
    .clk(and_1_out), .D(control_unit_1_fgi_2), .Q(FGI_q), .en(control_unit_1_fgiload));  // open: Qn, preset, reset
  D_Flip_Flop FGO (
    .clk(and_1_out), .D(control_unit_1_fgo_2), .Q(FGO_q), .en(control_unit_1_fgoload));  // open: Qn, preset, reset
  D_Flip_Flop IEN (.clk(and_1_out), .D(control_unit_1_ien), .en(control_unit_1_ienload));  // open: Q, Qn, preset, reset

  // Notes on the sheet:
  //   Mano Machine
  //   Common Bus
  //   AC
  //   IR
  //   PC
  //   DR
  //   FLAGS
  //   Nihal Rajpal
  //   (220283107028)
  //   Guided By: Prof. Zishan Noorani
endmodule

// CU
module Control_Unit (
  input  CLK,
  input  [3:0] SC,
  input  [15:0] IR,
  input  RESET,
  input  FGI,
  input  FGO,
  input  E,
  input  [15:0] AC,
  input  [15:0] DR,
  output FGOLOAD,
  output FGO_2,
  output FGILOAD,
  output FGI_2,
  output INPLOAD,
  output ACINR,
  output ECLR,
  output ECMP,
  output IENLOAD,
  output IEN,
  output OUTRLOAD,
  output HLT,
  output [2:0] REGSEL,
  output DRLOAD,
  output ARLOAD,
  output IRLOAD,
  output MLOAD,
  output PCLOAD,
  output PCINR,
  output ARINR,
  output DCINR,
  output ACCLR,
  output ELOAD,
  output ACLOAD,
  output [4:0] OPR
);

  wire and_3_out, and_4_out, and_5_out, and_6_out, and_7_out, and_8_out, and_9_out, buffer_1_out,
       comparator_1_eq, multiplexer_4_out, multiplexer_5_out, multiplexer_7_out, multiplexer_9_out,
       multiplexer_10_out, or_3_out, xnor_1_out, xnor_2_out;
  wire [1:0] and_1_out, or_2_out, rom_1_data;
  wire [3:0] priority_encoder_1_out;
  wire [4:0] adder_1_out, bit_extender_1_out, multiplexer_1_out, multiplexer_3_out;
  wire [6:0] adder_2_out, CMAR_q, multiplexer_6_out, multiplexer_8_out, multiplexer_11_out, rom_1_data_2,
       SBR_q;
  wire [15:0] multiplexer_2_out;
  wire [31:28] rom_1_data_3;

  and and_1 (and_1_out[0], IR[12], IR[13], IR[14]);
  Priority_Encoder #(.select(4)) priority_encoder_1 (
    .in0(IR[11]), .in1(IR[10]), .in2(IR[9]), .in3(IR[8]), .in4(IR[7]), .in5(IR[6]), .in6(IR[5]), .in7(IR[4]),
    .in8(IR[3]), .in9(IR[2]), .in10(IR[1]), .in11(IR[0]), .out(priority_encoder_1_out));  // open: in12, in13, in14, in15, gs, en_out, en_in
  and and_2 (and_1_out[1], IR[15], and_1_out[0]);
  and and_3 (and_3_out, ~and_1_out[0], IR[15]);  // AND_Gate
  assign bit_extender_1_out = {{1{1'b0}}, priority_encoder_1_out};  // Bit_Extender bit_extender_1
  Multiplexer #(.select(2), .width(5), .enable("false")) multiplexer_1 (
    .in0({5{1'b0}}), .in1(5'b00111), .in3(5'b10011), .out(multiplexer_1_out), .sel(and_1_out));  // open: in2
  Multiplexer #(.width(16), .enable("false")) multiplexer_2 (
    .in0(AC), .in1(DR), .out(multiplexer_2_out), .sel(rom_1_data[0]));
  Multiplexer #(.width(5), .enable("false")) multiplexer_3 (
    .in0({2'b00, IR[14:12]}), .in1(adder_1_out), .out(multiplexer_3_out), .sel(and_1_out[0]));
  Adder #(.width(5)) adder_1 (.a(bit_extender_1_out), .b(multiplexer_1_out), .out(adder_1_out));  // open: cin, cout
  Comparator #(.width(16)) comparator_1 (.a({16{1'b0}}), .b(multiplexer_2_out), .eq(comparator_1_eq));  // open: gt, lt
  xnor xnor_1 (xnor_1_out, AC[15], rom_1_data_3[31]);
  Multiplexer #(.select(2), .enable("false")) multiplexer_4 (
    .in0(1'b1), .in1(FGI), .in2(FGO), .in3(E), .out(multiplexer_4_out), .sel(rom_1_data));
  xnor xnor_2 (xnor_2_out, multiplexer_4_out, rom_1_data_3[31]);
  Multiplexer #(.enable("false")) multiplexer_5 (
    .in0(and_3_out), .in1(xnor_1_out), .out(multiplexer_5_out), .sel(rom_1_data[0]));
  Multiplexer #(.select(2), .width(7), .enable("false")) multiplexer_6 (
    .in0(adder_2_out), .in1(rom_1_data_2), .in2(SBR_q), .in3({multiplexer_3_out, 2'b00}),
    .out(multiplexer_6_out), .sel(or_2_out));
  Multiplexer #(.enable("false")) multiplexer_7 (
    .in0(comparator_1_eq), .in1(multiplexer_5_out), .out(multiplexer_7_out), .sel(rom_1_data[1]));
  Multiplexer #(.width(7), .enable("false")) multiplexer_8 (
    .in0(multiplexer_6_out), .in1(7'b1100100), .out(multiplexer_8_out), .sel(buffer_1_out));
  Multiplexer #(.enable("false")) multiplexer_9 (.in0(CLK), .in1(RESET), .out(multiplexer_9_out), .sel(RESET));
  buf buffer_1 (buffer_1_out, RESET);
  or or_1 (or_2_out[1], and_4_out, and_5_out);
  Multiplexer #(.enable("false")) multiplexer_10 (
    .in0(xnor_2_out), .in1(multiplexer_7_out), .out(multiplexer_10_out), .sel(rom_1_data_3[28]));
  and and_4 (and_4_out, ~multiplexer_10_out, rom_1_data_3[30]);  // AND_Gate
  Register #(.width(7), .trigger("falling")) CMAR (
    .D(multiplexer_8_out), .Q(CMAR_q), .clk(multiplexer_9_out));  // open: en, clr
  or or_2 (or_2_out[0], and_6_out, and_7_out);
  and and_5 (and_5_out, rom_1_data_3[30], ~rom_1_data_3[29]);  // AND_Gate
  and and_6 (and_6_out, rom_1_data_3[30], rom_1_data_3[29]);
  Adder #(.width(7)) adder_2 (.a(CMAR_q), .b(7'b0000001), .out(adder_2_out));  // open: cin, cout
  and and_7 (and_7_out, ~rom_1_data_3[30], multiplexer_10_out);  // AND_Gate
  Multiplexer #(.width(7), .enable("false")) multiplexer_11 (
    .in0(adder_2_out), .in1({multiplexer_3_out, 2'b00}), .out(multiplexer_11_out), .sel(and_8_out));
  Register #(.width(7), .trigger("falling")) SBR (
    .D(multiplexer_11_out), .en(or_3_out), .Q(SBR_q), .clk(CLK));  // open: clr
  ROM #(.addrWidth(7), .dataWidth(32)) rom_1 (
    .addr(CMAR_q),
    .data({rom_1_data_3, rom_1_data, rom_1_data_2, OPR, ACLOAD, ELOAD, ACCLR, DCINR, ARINR, PCINR, PCLOAD, MLOAD, IRLOAD, ARLOAD, DRLOAD, REGSEL}));  // open: sel
  or or_3 (or_3_out, and_9_out, and_8_out);
  and and_8 (and_8_out, rom_1_data_3[29], rom_1_data_3[30], multiplexer_10_out);
  and and_9 (and_9_out, ~rom_1_data_3[30], rom_1_data_3[29]);  // AND_Gate
  ROM #(.addrWidth(7), .dataWidth(12)) rom_2 (
    .addr(CMAR_q),
    .data({HLT, OUTRLOAD, IEN, IENLOAD, ECMP, ECLR, ACINR, INPLOAD, FGI_2, FGILOAD, FGO_2, FGOLOAD}));  // open: sel

  // Notes on the sheet:
  //   Mapping Logic
  //   Memory Indirect (I)
  //   Sequencing Logic
  //   Control Memory
  //   contents of rom_1 (hex, n*v repeats v):
  //   f 83222000 0 0 f 83203000 0 0 f 8320a003 0 0 83200044 0 0 0 83200081 0 0 0 242 83200081 0 0 f 400
  //   37e80043 83200000 83200800 0 0 0 83200000 0 0 0 8322e000 0 0 0 83201000 0 0 0 83243000 0 0 0
  //   83263000 0 0 0 83200000 0 0 0 3fe80000 83200000 0 0 bfe80000 83200000 0 0 33e80000 83200000 0 0
  //   2fe80000 83200000 6*0 83202000 0 0 0 83200004 0 0 0 a7e80000 83200000 0 0 abe80000 83200000 0 0
  //   83200000 0 0 0 83200000 0 0 0 12 127 7bf00015 22*0 40000100 40000017
  //   contents of rom_2 (hex, n*v repeats v):
  //   32*0 40 7*0 80 11*0 20 19*0 800 0 0 0 14 0 0 0 400 11*0 300 0 0 0 400
endmodule

module ALU (
  input  [15:0] B,
  input  [15:0] A,
  input  SHL,
  input  [4:0] OPR,
  input  SHR,
  output E,
  output [15:0] out_7
);

  wire adder_1_cout;
  wire [15:0] adder_1_out, and_1_out, multiplexer_1_out, multiplexer_2_out, nor_1_out, not_1_out, not_2_out,
       not_3_out, or_1_out;

  assign nor_1_out = ~(A | A);  // NOR_Gate nor_1, 16 bits wide
  assign not_1_out = ~A;  // NOT_Gate not_1, 16 bits wide
  assign or_1_out = A | A;  // OR_Gate or_1, 16 bits wide
  assign not_2_out = ~A;  // NOT_Gate not_2, 16 bits wide
  assign not_3_out = ~{16{1'b1}};  // NOT_Gate not_3, 16 bits wide
  Multiplexer #(.select(2), .width(16), .enable("false")) multiplexer_1 (
    .in0(A), .in1(not_2_out), .in2(not_3_out), .in3({16{1'b1}}), .out(multiplexer_1_out), .sel(OPR[1:0]));
  assign and_1_out = A & A;  // AND_Gate and_1, 16 bits wide
  Multiplexer #(.select(2), .width(16), .enable("false")) multiplexer_2 (
    .in0(and_1_out), .in1(or_1_out), .in2(nor_1_out), .in3(not_1_out), .out(multiplexer_2_out), .sel(OPR[1:0]));
  Adder #(.width(16)) adder_1 (.a(B), .b(multiplexer_1_out), .out(adder_1_out), .cin(OPR[2]), .cout(adder_1_cout));
  Multiplexer #(.select(2), .enable("false")) multiplexer_3 (
    .in0(adder_1_cout), .in1(OPR[2]), .in2(A[0]), .in3(A[15]), .out(E), .sel(OPR[4:3]));
  Multiplexer #(.select(2), .width(16), .enable("false")) multiplexer_4 (
    .in0(adder_1_out), .in1(multiplexer_2_out), .in2({SHR, A[15:1]}), .in3({A[14:0], SHL}), .out(out_7),
    .sel(OPR[4:3]));

  // Notes on the sheet:
  //   Arithmetic & Logic Unit
  //   Result
endmodule

// 16 bit Register
module DR (
  input  [15:0] Data_Input,
  input  INR,
  input  LD,
  input  CLK,
  input  CLR,
  output [15:0] Data_Output
);

  wire and_1_out, or_1_out;
  wire [15:0] adder_1_out, multiplexer_1_out;

  Pull_Resistor pull_resistor_1 (.node(INR));
  Multiplexer #(.width(16), .enable("false")) multiplexer_1 (
    .in0(Data_Input), .in1(adder_1_out), .out(multiplexer_1_out), .sel(INR));
  or or_1 (or_1_out, INR, LD);
  Register #(.width(16), .trigger("falling")) register_1 (
    .D(multiplexer_1_out), .en(or_1_out), .Q(Data_Output), .clk(CLK), .clr(and_1_out));
  and and_1 (and_1_out, CLK, CLR);
  Adder #(.width(16)) adder_1 (.a(Data_Output), .b(16'h1), .out(adder_1_out));  // open: cin, cout
endmodule

// 16 bit Register
module AC (
  input  [15:0] Data_Input,
  input  INPLOAD,
  input  [7:0] EXTERNAL_INP,
  input  INR,
  input  LD,
  input  CLK,
  input  CLR,
  output [15:0] Data_Output
);

  wire or_1_out;
  wire [15:0] adder_1_out, bit_extender_1_out, multiplexer_1_out, multiplexer_2_out;

  assign bit_extender_1_out = {{8{1'b0}}, EXTERNAL_INP};  // Bit_Extender bit_extender_1
  Pull_Resistor pull_resistor_1 (.node(INR));
  Multiplexer #(.width(16), .enable("false")) multiplexer_1 (
    .in0(Data_Input), .in1(bit_extender_1_out), .out(multiplexer_1_out), .sel(INPLOAD));
  Multiplexer #(.width(16), .enable("false")) multiplexer_2 (
    .in0(multiplexer_1_out), .in1(adder_1_out), .out(multiplexer_2_out), .sel(INR));
  or or_1 (or_1_out, INR, LD);
  Register #(.width(16), .trigger("falling")) register_1 (
    .D(multiplexer_2_out), .en(or_1_out), .Q(Data_Output), .clk(CLK), .clr(CLR));
  Adder #(.width(16)) adder_1 (.a(Data_Output), .b(16'h1), .out(adder_1_out));  // open: cin, cout
endmodule

// 16 bit Register
module IR (
  input  [15:0] Data_Input,
  input  INR,
  input  LD,
  input  CLK,
  input  CLR,
  output [15:0] Data_Output
);

  wire and_1_out, or_1_out;
  wire [15:0] adder_1_out, multiplexer_1_out;

  Pull_Resistor pull_resistor_1 (.node(INR));
  Multiplexer #(.width(16), .enable("false")) multiplexer_1 (
    .in0(Data_Input), .in1(adder_1_out), .out(multiplexer_1_out), .sel(INR));
  or or_1 (or_1_out, INR, LD);
  Register #(.width(16), .trigger("falling")) register_1 (
    .D(multiplexer_1_out), .en(or_1_out), .Q(Data_Output), .clk(CLK), .clr(and_1_out));
  and and_1 (and_1_out, CLK, CLR);
  Adder #(.width(16)) adder_1 (.a(Data_Output), .b(16'h1), .out(adder_1_out));  // open: cin, cout
endmodule

// 12 Bit Register
module AR (
  input  [15:0] Data_Input,
  input  LD,
  input  CLK,
  input  CLR,
  input  INR,
  output [11:0] Data_Output__12,
  output [15:0] Data_Output__16
);

  wire or_1_out;
  wire [11:0] adder_1_out, bit_extender_1_out, multiplexer_1_out;

  Bit_Extender #(.in_width(16), .out_width(12)) bit_extender_1 (.in(Data_Input), .out(bit_extender_1_out));
  Pull_Resistor pull_resistor_1 (.node(INR));
  Multiplexer #(.width(12), .enable("false")) multiplexer_1 (
    .in0(bit_extender_1_out), .in1(adder_1_out), .out(multiplexer_1_out), .sel(INR));
  or or_1 (or_1_out, INR, LD);
  Register #(.width(12), .trigger("falling")) register_1 (
    .D(multiplexer_1_out), .en(or_1_out), .Q(Data_Output__12), .clk(CLK), .clr(CLR));
  Adder #(.width(12)) adder_1 (.a(Data_Output__12), .b(12'h1), .out(adder_1_out));  // open: cin, cout
  assign Data_Output__16 = {{4{1'b0}}, Data_Output__12};  // Bit_Extender bit_extender_2
endmodule

// 12 Bit Register
module PC (
  input  [15:0] Data_Input,
  input  INR,
  input  LD,
  input  CLK,
  input  CLR,
  output [15:0] Data_Output__16
);

  wire or_1_out;
  wire [11:0] adder_1_out, bit_extender_1_out, multiplexer_1_out, register_1_q;

  Bit_Extender #(.in_width(16), .out_width(12)) bit_extender_1 (.in(Data_Input), .out(bit_extender_1_out));
  Pull_Resistor pull_resistor_1 (.node(INR));
  Multiplexer #(.width(12), .enable("false")) multiplexer_1 (
    .in0(bit_extender_1_out), .in1(adder_1_out), .out(multiplexer_1_out), .sel(INR));
  or or_1 (or_1_out, INR, LD);
  Pull_Resistor pull_resistor_2 (.node(LD));
  Register #(.width(12), .trigger("falling")) register_1 (
    .D(multiplexer_1_out), .en(or_1_out), .Q(register_1_q), .clk(CLK), .clr(CLR));
  Adder #(.width(12)) adder_1 (.a(register_1_q), .b(12'h1), .out(adder_1_out));  // open: cin, cout
  assign Data_Output__16 = {{4{1'b0}}, register_1_q};  // Bit_Extender bit_extender_2
endmodule

// 16 bit Register
module TR (
  input  [15:0] Data_Input,
  input  INR,
  input  LD,
  input  CLK,
  input  CLR,
  output [15:0] Data_Output
);

  wire and_1_out, or_1_out;
  wire [15:0] adder_1_out, multiplexer_1_out;

  Pull_Resistor pull_resistor_1 (.node(INR));
  Multiplexer #(.width(16), .enable("false")) multiplexer_1 (
    .in0(Data_Input), .in1(adder_1_out), .out(multiplexer_1_out), .sel(INR));
  or or_1 (or_1_out, INR, LD);
  Register #(.width(16), .trigger("falling")) register_1 (
    .D(multiplexer_1_out), .en(or_1_out), .Q(Data_Output), .clk(CLK), .clr(and_1_out));
  and and_1 (and_1_out, CLK, CLR);
  Adder #(.width(16)) adder_1 (.a(Data_Output), .b(16'h1), .out(adder_1_out));  // open: cin, cout
endmodule

// 8 bit Register
module INPR (
  input  [7:0] Data_Input,
  input  INR,
  input  LD,
  input  CLK,
  input  CLR,
  output [7:0] Data_Output
);

  wire and_1_out, or_1_out;
  wire [7:0] adder_1_out, multiplexer_1_out;

  Pull_Resistor pull_resistor_1 (.node(INR));
  Multiplexer #(.width(8), .enable("false")) multiplexer_1 (
    .in0(Data_Input), .in1(adder_1_out), .out(multiplexer_1_out), .sel(INR));
  or or_1 (or_1_out, INR, LD);
  Register register_1 (.D(multiplexer_1_out), .en(or_1_out), .Q(Data_Output), .clk(CLK), .clr(and_1_out));
  and and_1 (and_1_out, CLK, CLR);
  Adder adder_1 (.a(Data_Output), .b(8'h1), .out(adder_1_out));  // open: cin, cout
endmodule

// 8 bit Register
module OUTR (
  input  [7:0] Data_Input,
  input  INR,
  input  LD,
  input  CLK,
  input  CLR,
  output [7:0] Data_Output
);

  wire and_1_out, or_1_out;
  wire [7:0] adder_1_out, multiplexer_1_out;

  Pull_Resistor pull_resistor_1 (.node(INR));
  Multiplexer #(.width(8), .enable("false")) multiplexer_1 (
    .in0(Data_Input), .in1(adder_1_out), .out(multiplexer_1_out), .sel(INR));
  or or_1 (or_1_out, INR, LD);
  Register register_1 (.D(multiplexer_1_out), .en(or_1_out), .Q(Data_Output), .clk(CLK), .clr(and_1_out));
  and and_1 (and_1_out, CLK, CLR);
  Adder adder_1 (.a(Data_Output), .b(8'h1), .out(adder_1_out));  // open: cin, cout
endmodule

module SC (
  input  INR,
  input  CLK,
  input  CLR,
  output [3:0] Data_Output
);

  wire and_1_out;
  wire [3:0] adder_1_out;

  Register #(.width(4)) register_1 (.D(adder_1_out), .en(INR), .Q(Data_Output), .clk(CLK), .clr(and_1_out));
  and and_1 (and_1_out, CLK, CLR);
  Adder #(.width(4)) adder_1 (.a(Data_Output), .b(4'b0001), .out(adder_1_out));  // open: cin, cout
endmodule

module E_Flag (
  input  CLK,
  input  E,
  input  CLR,
  input  CMP,
  input  LOAD,
  output Q
);

  wire d_ff_1_qn, multiplexer_1_out;

  Multiplexer #(.enable("false")) multiplexer_1 (.in0(E), .in1(d_ff_1_qn), .out(multiplexer_1_out), .sel(CMP));
  D_Flip_Flop #(.trigger("falling")) d_ff_1 (
    .clk(CLK), .D(multiplexer_1_out), .Q(Q), .Qn(d_ff_1_qn), .en(LOAD), .reset(CLR));  // open: preset
endmodule

module _7_Segment_Decoder (
  input  [3:0] in_1,
  output A,
  output B,
  output C,
  output D,
  output E,
  output F,
  output G
);

  wire and_1_out, and_2_out, and_3_out, and_4_out, and_5_out, and_6_out, and_7_out, and_8_out, and_9_out,
       and_10_out, not_1_out, not_2_out, not_3_out;

  not not_1 (not_1_out, in_1[2]);
  not not_2 (not_2_out, in_1[1]);
  not not_3 (not_3_out, in_1[0]);
  and and_1 (and_1_out, not_1_out, not_3_out);
  and and_2 (and_2_out, in_1[2], in_1[0]);
  and and_3 (and_3_out, not_1_out, in_1[1]);
  and and_4 (and_4_out, in_1[1], not_3_out);
  and and_5 (and_5_out, in_1[2], not_3_out);
  and and_6 (and_6_out, in_1[2], not_2_out);
  and and_7 (and_7_out, not_1_out, in_1[1]);
  and and_8 (and_8_out, not_2_out, not_3_out);
  and and_9 (and_9_out, in_1[0], in_1[1]);
  and and_10 (and_10_out, in_1[2], not_2_out, in_1[0]);
  or or_1 (A, and_1_out, in_1[1], and_2_out, in_1[3]);
  or or_2 (B, and_8_out, not_1_out, and_9_out);
  or or_3 (D, and_1_out, in_1[3], and_3_out, and_4_out, and_10_out);
  or or_4 (E, and_1_out, and_4_out);
  or or_5 (F, in_1[3], and_5_out, and_6_out, and_8_out);
  or or_6 (G, and_6_out, and_7_out, and_5_out, in_1[3]);
  or or_7 (C, not_2_out, in_1[0], in_1[2]);
endmodule
